# Fritzing sketch ESP32_DS18B20_Oled_NMEA0183_2K (saved by Fritzing 1.0.4)

parts:
  M3 = RioRand LM2596
  J2 = Power Jack [package=power_jack_slot]
  U1 = ESP32S-HiLetgo [part_number=ESP32S-HiLetgo]
  Composant1 = Adafruit BME280
  R1 = Resistor [tolerance=±2% power=0.5W resistance=4.7k package=THT]
  DS1 = DS18B20 1-Wire Temperature Sensor [part_number=DS18B20]
  Composant2 = OLED Monochrome 128x32 I2C [part_number=931]
  S1 = Pushbutton [package="[THT]"]

nets:
  N1: M3.Pin_1, J2.PWR
  N2: M3.Pin_2, J2.GND
  VIN: M3.Pin_3, U1.VIN, Composant1.VIN, R1.Pin_1, DS1.VDD, Composant2.VIN
  GND: M3.Pin_4, U1.GND, Composant1.GND, DS1.GND, Composant2.GND, S1.Pin_1, S1.Pin_2
  N3: U1.GPIO4, R1.Pin_0, DS1.DQ
  N4: U1.GPIO17, S1.Pin_4
  N5: U1.GPIO21, Composant1.SDI/SDA, Composant2.SDA
  N6: U1.GPIO22, Composant1.SCK/SCL, Composant2.SCL

notes:
  5.2 volts
  7 à 14 volts

custom parts:
  ESP32S-HiLetgo: HiLetgo ESP-WROOM-32 ESP32 ESP-32S Development Board 2.4GHz Dual-Mode WiFi + Bluetooth Dual Cores Microcontroller The ESP32 integrated with Antenna switches, RF Balun, power amplifiers, low-noise amplifiers, filters, and management modules, and the entire solution occupies the least area of PCB. 2.4 GHz Wi-Fi plus Bluetooth dual-mode chip, with TSMC Ultra-low power consumption 40nm technology,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
  Adafruit BME280: Bosch has stepped up their game with their new BME280 sensor, an environmental sensor with temperature, barometric pressure and humidity! This sensor is great for all sorts of weather/environmental sensing and can even be used in both I2C and SPI! This precision sensor from Bosch is the best low-cost sensing solution for measuring humidity with ±3% accuracy, barometric pressure with ±1 hPa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
  OLED Monochrome 128x32 I2C: These displays are small, only about 1" diagonal, but very readable due to the high contrast of an OLED display. This display is made of 128x32 individual white OLED pixels, each one is turned on or off by the controller chip. Because the display makes its own light, no backlight is required. This reduces the power required to run the OLED and is why the display has such high contrast; we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
